# Fritzing sketch bathbuddy (saved by Fritzing 0.9.9b)
breadboards: 1

parts:
  U1 = ESP8266-01S [part_number=ESP8266]
  S1 = Momentary Switch [package=ksa_sealed_tac_switch]
  S2 = Momentary Switch [package=ksa_sealed_tac_switch]
  S3 = Momentary Switch [package=ksa_sealed_tac_switch]
  M1 = RioRand LM2596
  VCC1 = 4 x AAA Battery Mount

nets:
  N1: U1.RXD, S3.1
  N2: U1.VCC, U1.CH_PD, M1.Pin_3
  N3: U1.GPIO_0, S1.3
  N4: U1.GPIO_2, S2.3
  N5: U1.GND, S1.2, S2.2, S3.2, M1.Pin_4
  N6: M1.Pin_1, VCC1.+
  N7: M1.Pin_2, VCC1.-
